# Fritzing sketch schema (saved by Fritzing 0.9.3b)
breadboards: 1

parts:
  Componente1 = Arduino Uno (Rev3) - ICSP
  LED1 = smd LED [color="Red (633nm)" package="0603 [SMD]"]
  LED2 = smd LED [color="Blue (470nm)" package="0603 [SMD]"]
  R1 = Resistor [tolerance=±5% resistance=100 package="0603 [SMD]"]
  R2 = Resistor [tolerance=±5% resistance=100 package="0603 [SMD]"]
  J1 = Piezo Speaker  # not connected

nets:
  N1: Componente1.D8, R1.Pin_1
  N2: Componente1.GND, LED2.cathode
  N3: Componente1.D7, R2.Pin_1
  N4: LED1.anode, R1.Pin_0
  N5: LED2.anode, R2.Pin_0
